# Fritzing sketch assambly (saved by Fritzing 0.9.4)
breadboards: 1

parts:
  U1 = ESP8266 NodeMCU LoLin module
  OLED_I2C1 = OLED 128x64 I2C Monochrome Display
  M1 = BMP280
  R1 = Resistor [tolerance=±5% resistance=220 package=THT]  # not connected
  R2 = Resistor [tolerance=±5% resistance=220 package=THT]  # not connected
  R3 = Resistor [tolerance=±5% resistance=220 package=THT]  # not connected
  LED1 = RGB LED (com. cathode, rgb) [package="5 mm [THT]"]
  LED2 = smd LED [color="Red (633nm)" package="1206 [SMD]"]
  R4 = Resistor [tolerance=±5% resistance=220 package=THT]
  LED3 = smd LED [color="Green (555nm)" package="1206 [SMD]"]
  R5 = Resistor [tolerance=±5% resistance=220 package=THT]
  VCC1 = Battery block 9V
  KY-1 = Keyes Relay [package=THT]

nets:
  N1: U1.D1, OLED_I2C1.SCK, M1.SCL
  N2: U1.D2, OLED_I2C1.SDA, M1.SDA
  N3: U1.D3, KY-1.signal
  3V3: U1.3V3, OLED_I2C1.VDD, M1.VIN, R4.Pin_1, KY-1.power
  GND: U1.GND, OLED_I2C1.GND, M1.GND, LED1.common_cathode, LED2.cathode, LED3.cathode, VCC1.-, KY-1.ground
  N4: U1.D5, R5.Pin_0
  N5: U1.D6, LED1.red_anode
  N6: U1.D7, LED1.green_anode
  N7: U1.Vin, VCC1.+
  N8: LED2.anode, KY-1.NO
  N9: R4.Pin_0, KY-1.C
  N10: LED3.anode, R5.Pin_1

custom parts:
  ESP8266 NodeMCU LoLin module: ESP8266 based NodeMCU
  BMP280: Temperature Humidity Barometric presure Sensor, I2C
  Keyes Relay: The Keyes 5V relay module is suitable for SCM development, home appliance control. It uses a 5V~12V TIL control signal which can control DC / AC signal.
